// Logisim project Microprocessor.circ as structural Verilog: 1 circuit, main circuit main
module main (
  input  [3:0] in_1,
  input  [3:0] in_2,
  input  [3:0] in_3,
  input  [3:0] in_4,
  input  [3:0] in_5,
  input  [3:0] in_6,
  input  [3:0] in_7,
  input  [3:0] in_8,
  input  Clock,
  input  Reset
);

  wire and_1_out, and_2_out, and_3_out, and_4_out, and_5_out, and_6_out, and_7_out, and_8_out, and_9_out,
       and_10_out, and_11_out, main_4_p14, main_4_p15;
  wire [1:0] register_2_q;
  wire [3:0] main_1_p4, main_1_p9, main_2_p4, main_2_p8, main_2_p16, main_3_p13, register_1_q, register_4_q,
       register_6_q, register_7_q;
  wire [7:0] main_4_p6;
  wire [15:0] rom_1_data;

  // INC_4_main main_1: pin names not known; wires that end beside it: main_1_p4[3], main_1_p4[2], main_1_p4[1], main_1_p4[0], 1'b1, main_1_p9[3], main_1_p9[2], main_1_p9[1], main_1_p9[0]
  Hex_Digit_Display hex_digit_display_1 (.value(rom_1_data[15:12]));  // open: dp
  Register #(.width(4)) register_1 (.D(main_2_p4), .en(rom_1_data[2]), .Q(register_1_q), .clk(Clock), .clr(Reset));
  Register #(.width(2)) register_2 (.D(rom_1_data[1:0]), .en(1'b1), .Q(register_2_q), .clk(Clock), .clr(Reset));
  Register #(.width(4)) register_3 (.D(main_1_p9), .en(rom_1_data[8]), .Q(main_1_p4), .clk(Clock), .clr(Reset));
  Register #(.width(4)) register_4 (.D(main_2_p4), .en(rom_1_data[7]), .Q(register_4_q), .clk(Clock), .clr(Reset));
  Hex_Digit_Display hex_digit_display_2 (.value(rom_1_data[7:4]));  // open: dp
  Hex_Digit_Display hex_digit_display_3 (.value(rom_1_data[11:8]));  // open: dp
  Hex_Digit_Display hex_digit_display_4 (.value(main_1_p4));  // open: dp
  Hex_Digit_Display hex_digit_display_5 (.value(register_4_q));  // open: dp
  Hex_Digit_Display hex_digit_display_6 (.value(rom_1_data[3:0]));  // open: dp
  Hex_Digit_Display hex_digit_display_7 (.value(register_1_q));  // open: dp
  Hex_Digit_Display hex_digit_display_8 (.value({2'b00, register_2_q}));  // open: dp
  // ALU_main main_2: pin names not known; wires that end beside it: main_2_p4[3], main_2_p4[2], main_2_p4[1], main_2_p4[0], main_2_p8[3], main_2_p8[2], main_2_p8[1], main_2_p8[0], 1'b0, rom_1_data[11], rom_1_data[10], rom_1_data[9], main_2_p16[3], main_2_p16[2], main_2_p16[1], main_2_p16[0], rom_1_data[6]
  // MUX_4_main main_3: pin names not known; wires that end beside it: rom_1_data[8], main_1_p4[3], main_1_p4[2], main_1_p4[1], main_1_p4[0], register_4_q[3], register_4_q[2], register_4_q[1], register_4_q[0], main_3_p13[3], main_3_p13[2], main_3_p13[1], main_3_p13[0]
  Hex_Digit_Display hex_digit_display_9 (.value(main_2_p16));  // open: dp
  Hex_Digit_Display hex_digit_display_10 (.value(main_3_p13));  // open: dp
  Register #(.width(4)) register_5 (.D(main_2_p16), .en(rom_1_data[6]), .Q(main_2_p8), .clk(Clock), .clr(Reset));
  ROM #(.addrWidth(6), .dataWidth(16)) rom_1 (.addr({register_1_q, register_2_q}), .data(rom_1_data));  // open: sel
  Hex_Digit_Display hex_digit_display_11 (.value(main_2_p8));  // open: dp
  assign main_2_p4 = rom_1_data[5] ? main_2_p8 : 4'bz;  // Controlled_Buffer controlled_buffer_1
  // DECODER_4_main main_4: pin names not known; wires that end beside it: main_3_p13[3], main_3_p13[2], main_3_p13[1], main_3_p13[0], 1'b1, main_4_p6[0], main_4_p6[1], main_4_p6[2], main_4_p6[3], main_4_p6[4], main_4_p6[5], main_4_p6[6], main_4_p6[7], main_4_p14, main_4_p15
  and and_1 (and_1_out, main_4_p14, rom_1_data[3]);
  and and_2 (and_2_out, main_4_p15, rom_1_data[3]);
  and and_3 (and_3_out, main_4_p15, rom_1_data[4]);
  Register #(.width(4)) register_6 (.D(main_2_p4), .en(and_1_out), .Q(register_6_q), .clk(Clock), .clr(Reset));
  Register #(.width(4)) register_7 (.D(main_2_p4), .en(and_2_out), .Q(register_7_q), .clk(Clock), .clr(Reset));
  Hex_Digit_Display hex_digit_display_12 (.value(register_6_q));  // open: dp
  assign main_2_p4 = and_3_out ? register_7_q : 4'bz;  // Controlled_Buffer controlled_buffer_2
  and and_4 (and_4_out, rom_1_data[4], main_4_p6[0]);
  and and_5 (and_5_out, rom_1_data[4], main_4_p6[1]);
  and and_6 (and_6_out, rom_1_data[4], main_4_p6[2]);
  and and_7 (and_7_out, rom_1_data[4], main_4_p6[3]);
  Hex_Digit_Display hex_digit_display_13 (.value(main_2_p4));  // open: dp
  assign main_2_p4 = and_4_out ? in_1 : 4'bz;  // Controlled_Buffer controlled_buffer_3
  assign main_2_p4 = and_5_out ? in_3 : 4'bz;  // Controlled_Buffer controlled_buffer_4
  assign main_2_p4 = and_6_out ? in_5 : 4'bz;  // Controlled_Buffer controlled_buffer_5
  assign main_2_p4 = and_7_out ? in_7 : 4'bz;  // Controlled_Buffer controlled_buffer_6
  and and_8 (and_8_out, rom_1_data[4], main_4_p6[4]);
  and and_9 (and_9_out, rom_1_data[4], main_4_p6[5]);
  and and_10 (and_10_out, rom_1_data[4], main_4_p6[6]);
  and and_11 (and_11_out, rom_1_data[4], main_4_p6[7]);
  assign main_2_p4 = and_8_out ? in_2 : 4'bz;  // Controlled_Buffer controlled_buffer_7
  assign main_2_p4 = and_9_out ? in_4 : 4'bz;  // Controlled_Buffer controlled_buffer_8
  assign main_2_p4 = and_10_out ? in_6 : 4'bz;  // Controlled_Buffer controlled_buffer_9
  assign main_2_p4 = and_11_out ? in_8 : 4'bz;  // Controlled_Buffer controlled_buffer_10

  // Notes on the sheet:
  //   Program Counter Register
  //   Memory Address Register
  //   Data Bus
  //   Feedback Path
  //   Accumulator Register
  //   contents of rom_1 (hex, n*v repeats v):
  //   115 550 0 0 1115 350 0 0 115 1
  //   Address Bus
  //   Memory Select
  //   Memory Select Lines
  //   1 x 4-bit Output Port
  //   1x 4-bit RAM
  //   Data Bus
  //   8 x 4-bit ROM
endmodule
